// Logisim project alu.circ as structural Verilog: 1 circuit, main circuit main
module main (
  input  [31:0] X,
  input  [31:0] Y,
  input  [3:0] Switch,
  input  in_4,
  input  [30:0] in_5,
  input  [30:0] in_6,
  output Signed_Overflow,
  output Equal,
  output [31:0] Result
);

  wire addoverflow, slt, sltu, suboverflow;
  wire [4:0] x_5;
  wire [31:0] add, addu, \and , \or , sll, sra, srl, sub, subu;

  Bit_Extender #(.in_width(32), .out_width(5)) bit_extender_1 (.in(X), .out(x_5));
  Shifter #(.width(32)) shifter_1 (.in(Y), .\dist (x_5), .out(sll));
  Shifter #(.width(32), .shift("lr")) shifter_2 (.in(Y), .\dist (x_5), .out(srl));
  Shifter #(.width(32), .shift("ar")) shifter_3 (.in(Y), .\dist (x_5), .out(sra));
  Adder #(.width(32)) adder_1 (.a(X), .b(Y), .out(add), .cout(addoverflow));  // open: cin
  Adder #(.width(32)) adder_2 (.a(X), .b(Y), .out(addu));  // open: cin, cout
  Subtractor #(.width(32)) subtractor_1 (.a(X), .b(Y), .out(sub), .bout(suboverflow));  // open: bin
  Subtractor #(.width(32)) subtractor_2 (.a(X), .b(Y), .out(subu));  // open: bin, bout
  assign \and  = X & Y;  // AND_Gate and_1, 32 bits wide
  assign \or  = X | Y;  // OR_Gate or_1, 32 bits wide
  Comparator #(.width(32)) comparator_1 (.a(X), .b(Y), .eq(Equal), .lt(slt));  // open: gt
  Comparator #(.width(32), .mode("unsigned")) comparator_2 (.a(X), .b(Y), .lt(sltu));  // open: gt, eq
  Multiplexer #(.select(4), .width(32)) multiplexer_1 (
    .in0(sll), .in1(srl), .in2(sra), .in5(add), .in6(addu), .in7(sub), .in8(subu), .in9(\and ), .in10(\or ),
    .in11({in_5, slt}), .in12({in_6, sltu}), .out(Result), .sel(Switch));  // open: in3, in4, in13, in14, in15, en
  Multiplexer #(.select(4)) multiplexer_2 (
    .in0(in_4), .in1(in_4), .in2(in_4), .in3(in_4), .in4(in_4), .in5(addoverflow), .in6(in_4),
    .in7(suboverflow), .in8(in_4), .in9(in_4), .in10(in_4), .in11(in_4), .in12(in_4), .in13(in_4),
    .in14(in_4), .in15(in_4), .out(Signed_Overflow), .sel(Switch));  // open: en

  // Other names for the same wires on the sheet: overflow = Signed_Overflow; S[3:0] = Switch;
  //   sltuval[31:0] = {in_6, sltu}; sltval[31:0] = {in_5, slt}

  // Notes on the sheet:
  //   INPUTS to your circuit
  //   DON'T CHANGE THE LOCATIONS OF THE INPUTS AND OUTPUTS!
  //   OUTPUTS from your circuit
endmodule
