// Logisim project alu.circ as structural Verilog: 1 circuit, main circuit main
module main (
  input  [31:0] X,
  input  [31:0] Y,
  input  [3:0] Switch,
  output Signed_Overflow,
  output Equal,
  output [31:0] Result
);

  wire addoverflow, carry1, carry1s, carry2, carry2s, slt, sltu, suboverflow;
  wire [4:0] x_5;
  wire [31:0] add, addu, \and , \or , sll, sra, srl, sub, subu;

  Bit_Extender #(.in_width(32), .out_width(5)) bit_extender_1 (.in(X), .out(x_5));
  Subtractor #(.width(1)) subtractor_1 (.a(X[31]), .b(Y[31]), .out(sub[31]), .bin(carry1s), .bout(carry2s));
  Subtractor #(.width(31)) subtractor_2 (.a(X[30:0]), .b(Y[30:0]), .out(sub[30:0]), .bout(carry1s));  // open: bin
  Adder #(.width(1)) adder_1 (.a(X[31]), .b(Y[31]), .out(add[31]), .cin(carry1), .cout(carry2));
  Adder #(.width(31)) adder_2 (.a(X[30:0]), .b(Y[30:0]), .out(add[30:0]), .cout(carry1));  // open: cin
  Shifter #(.width(32)) shifter_1 (.in(Y), .\dist (x_5), .out(sll));
  Shifter #(.width(32), .shift("lr")) shifter_2 (.in(Y), .\dist (x_5), .out(srl));
  Shifter #(.width(32), .shift("ar")) shifter_3 (.in(Y), .\dist (x_5), .out(sra));
  Adder #(.width(32)) adder_3 (.a(X), .b(Y), .out(addu));  // open: cin, cout
  Subtractor #(.width(32)) subtractor_3 (.a(X), .b(Y), .out(subu));  // open: bin, bout
  assign \and  = X & Y;  // AND_Gate and_1, 32 bits wide
  assign \or  = X | Y;  // OR_Gate or_1, 32 bits wide
  Comparator #(.width(32)) comparator_1 (.a(X), .b(Y), .eq(Equal), .lt(slt));  // open: gt
  Comparator #(.width(32), .mode("unsigned")) comparator_2 (.a(X), .b(Y), .lt(sltu));  // open: gt, eq
  xor xor_1 (addoverflow, carry2, carry1);
  xor xor_2 (suboverflow, carry2s, carry1s);
  Multiplexer #(.select(4), .width(32)) multiplexer_1 (
    .in0(sll), .in1(srl), .in2(sra), .in3({32{1'b0}}), .in4({32{1'b0}}), .in5(add), .in6(addu), .in7(sub),
    .in8(subu), .in9(\and ), .in10(\or ), .in11({{31{1'b0}}, slt}), .in12({{31{1'b0}}, sltu}),
    .in13({32{1'b0}}), .in14({32{1'b0}}), .in15({32{1'b0}}), .out(Result), .sel(Switch));  // open: en
  Multiplexer #(.select(4), .disabled(0)) multiplexer_2 (
    .in0(1'b0), .in1(1'b0), .in2(1'b0), .in3(1'b0), .in4(1'b0), .in5(addoverflow), .in6(1'b0),
    .in7(suboverflow), .in8(1'b0), .in9(1'b0), .in10(1'b0), .in11(1'b0), .in12(1'b0), .in13(1'b0),
    .in14(1'b0), .in15(1'b0), .out(Signed_Overflow), .sel(Switch));  // open: en

  // Other names for the same wires on the sheet: overflow = Signed_Overflow; S[3:0] = Switch; sltuval[0] = sltu;
  //   sltval[0] = slt; X31[30:0] = X[30:0]; X1 = X[31]; Y31[30:0] = Y[30:0]; Y1 = Y[31]

  // Notes on the sheet:
  //   INPUTS to your circuit
  //   DON'T CHANGE THE LOCATIONS OF THE INPUTS AND OUTPUTS!
  //   OUTPUTS from your circuit
endmodule
