// Logisim project regfile.circ as structural Verilog: 1 circuit, main circuit main
module main (
  input  in_1,
  input  [4:0] Read_Register_1,
  input  [4:0] Read_Register_2,
  input  [4:0] Write_Register,
  input  [31:0] Write_Data,
  input  Write_Enable,
  input  Clock,
  output [31:0] s0_Value,
  output [31:0] s1_Value,
  output [31:0] s2_Value,
  output [31:0] ra_Value,
  output [31:0] sp_Value,
  output [31:0] Read_Data_1,
  output [31:0] Read_Data_2
);

  wire [31:0] _0, _1, _2, _3, _4, _5, _6, _7, _8, _9, _10, _11, _12, _13, _14, _15, _19, _20, _21, _22, _23,
       _24, _25, _26, _27, _28, _30;

  Register #(.width(32)) register_1 (.en(in_1), .Q(_0), .clk(Clock));  // open: D, clr
  Register #(.width(32)) register_2 (.D(Write_Data), .en(Write_Enable), .Q(_3), .clk(Clock));  // open: clr
  Register #(.width(32)) register_3 (.D(Write_Data), .en(Write_Enable), .Q(_11), .clk(Clock));  // open: clr
  Register #(.width(32)) register_4 (.D(Write_Data), .en(Write_Enable), .Q(_19), .clk(Clock));  // open: clr
  Register #(.width(32)) register_5 (.D(Write_Data), .en(Write_Enable), .Q(_1), .clk(Clock));  // open: clr
  Register #(.width(32)) register_6 (.D(Write_Data), .en(Write_Enable), .Q(_2), .clk(Clock));  // open: clr
  Register #(.width(32)) register_7 (.D(Write_Data), .en(Write_Enable), .Q(_4), .clk(Clock));  // open: clr
  Register #(.width(32)) register_8 (.D(Write_Data), .en(Write_Enable), .Q(_12), .clk(Clock));  // open: clr
  Register #(.width(32)) register_9 (.D(Write_Data), .en(Write_Enable), .Q(_20), .clk(Clock));  // open: clr
  Register #(.width(32)) register_10 (.D(Write_Data), .en(Write_Enable), .Q(_5), .clk(Clock));  // open: clr
  Demultiplexer #(.select(5), .width(32)) demultiplexer_1 (
    .out0(_0), .out1(_1), .out2(_2), .out3(_3), .out4(_4), .out5(_5), .out6(_6), .out7(_7), .out8(_8),
    .out9(_9), .out10(_10), .out11(_11), .out12(_12), .out13(_13), .out14(_14), .out15(_15),
    .out16(s0_Value), .out17(s1_Value), .out18(s2_Value), .out19(_19), .out20(_20), .out21(_21), .out22(_22),
    .out23(_23), .out24(_24), .out25(_25), .out26(_26), .out27(_27), .out28(_28), .out29(ra_Value),
    .out30(_30), .out31(sp_Value), .in(Write_Data), .sel(Write_Register));  // open: en
  Register #(.width(32)) register_11 (.D(Write_Data), .en(Write_Enable), .Q(_13), .clk(Clock));  // open: clr
  Register #(.width(32)) register_12 (.D(Write_Data), .en(Write_Enable), .Q(_21), .clk(Clock));  // open: clr
  Register #(.width(32)) register_13 (.D(Write_Data), .en(Write_Enable), .Q(_27), .clk(Clock));  // open: clr
  Register #(.width(32)) register_14 (.D(Write_Data), .en(Write_Enable), .Q(_14), .clk(Clock));  // open: clr
  Register #(.width(32)) register_15 (.D(Write_Data), .en(Write_Enable), .Q(_22), .clk(Clock));  // open: clr
  Register #(.width(32)) register_16 (.D(Write_Data), .en(Write_Enable), .Q(_28), .clk(Clock));  // open: clr
  Multiplexer #(.select(5), .width(32)) multiplexer_1 (
    .in0(_0), .in1(_1), .in2(_2), .in3(_3), .in4(_4), .in5(_5), .in6(_6), .in7(_7), .in8(_8), .in9(_9),
    .in10(_10), .in11(_11), .in12(_12), .in13(_13), .in14(_14), .in15(_15), .in16(s0_Value), .in17(s1_Value),
    .in18(s2_Value), .in19(_19), .in20(_20), .in21(_21), .in22(_22), .in23(_23), .in24(_24), .in25(_25),
    .in26(_26), .in27(_27), .in28(_28), .in29(ra_Value), .in30(_30), .in31(sp_Value), .out(Read_Data_1),
    .sel(Read_Register_1));  // open: en
  Register #(.width(32)) register_17 (.D(Write_Data), .en(Write_Enable), .Q(_15), .clk(Clock));  // open: clr
  Register #(.width(32)) register_18 (.D(Write_Data), .en(Write_Enable), .Q(_23), .clk(Clock));  // open: clr
  Register #(.width(32)) register_19 (.D(Write_Data), .en(Write_Enable), .Q(ra_Value), .clk(Clock));  // open: clr
  Register #(.width(32)) register_20 (.D(Write_Data), .en(Write_Enable), .Q(_6), .clk(Clock));  // open: clr
  Multiplexer #(.select(5), .width(32)) multiplexer_2 (
    .in0(_0), .in1(_1), .in2(_2), .in3(_3), .in4(_4), .in5(_5), .in6(_6), .in7(_7), .in8(_8), .in9(_9),
    .in10(_10), .in11(_11), .in12(_12), .in13(_13), .in14(_14), .in15(_15), .in16(s0_Value), .in17(s1_Value),
    .in18(s2_Value), .in19(_19), .in20(_20), .in21(_21), .in22(_22), .in23(_23), .in24(_24), .in25(_25),
    .in26(_26), .in27(_27), .in28(_28), .in29(ra_Value), .in30(_30), .in31(sp_Value), .out(Read_Data_2),
    .sel(Read_Register_2));  // open: en
  Register #(.width(32)) register_21 (.D(Write_Data), .en(Write_Enable), .Q(s0_Value), .clk(Clock));  // open: clr
  Register #(.width(32)) register_22 (.D(Write_Data), .en(Write_Enable), .Q(_24), .clk(Clock));  // open: clr
  Register #(.width(32)) register_23 (.D(Write_Data), .en(Write_Enable), .Q(_30), .clk(Clock));  // open: clr
  Register #(.width(32)) register_24 (.D(Write_Data), .en(Write_Enable), .Q(_7), .clk(Clock));  // open: clr
  Register #(.width(32)) register_25 (.D(Write_Data), .en(Write_Enable), .Q(_8), .clk(Clock));  // open: clr
  Register #(.width(32)) register_26 (.D(Write_Data), .en(Write_Enable), .Q(s1_Value), .clk(Clock));  // open: clr
  Register #(.width(32)) register_27 (.D(Write_Data), .en(Write_Enable), .Q(_25), .clk(Clock));  // open: clr
  Register #(.width(32)) register_28 (.D(Write_Data), .en(Write_Enable), .Q(sp_Value), .clk(Clock));  // open: clr
  Register #(.width(32)) register_29 (.D(Write_Data), .en(Write_Enable), .Q(_9), .clk(Clock));  // open: clr
  Register #(.width(32)) register_30 (.D(Write_Data), .en(Write_Enable), .Q(_10), .clk(Clock));  // open: clr
  Register #(.width(32)) register_31 (.D(Write_Data), .en(Write_Enable), .Q(s2_Value), .clk(Clock));  // open: clr
  Register #(.width(32)) register_32 (.D(Write_Data), .en(Write_Enable), .Q(_26), .clk(Clock));  // open: clr

  // Other names for the same wires on the sheet: _16[31:0] = s0_Value; _17[31:0] = s1_Value; _18[31:0] = s2_Value;
  //   _29[31:0] = ra_Value; _31[31:0] = sp_Value; clk = Clock; read_data1[31:0] = Read_Data_1;
  //   read_data2[31:0] = Read_Data_2; read_reg1[4:0] = Read_Register_1; read_reg2[4:0] = Read_Register_2;
  //   write_en = Write_Enable; write_reg[4:0] = Write_Register

  // Notes on the sheet:
  //   INPUTS to your circuit
  //   DON'T CHANGE THE LOCATIONS OF THE INPUTS AND OUTPUTS!
  //   These are DEBUG/TEST outputs from your circuit.
  //   OUTPUTS from your circuit
endmodule
